# Fritzing sketch rmft-stage1-pin-turnouts (saved by Fritzing 0.9.10b)

parts:
  Part1 = Arduino Mega 2560 (Rev3)
  Part2 = Arduino Motor Shield (Rev3)  # not connected
  M1 = fc-51 [package=THT]
  M2 = fc-51 [package=THT]
  M3 = fc-51 [package=THT]
  M4 = fc-51 [package=THT]
  M5 = fc-51 [package=THT]
  M6 = fc-51 [package=THT]

nets:
  N1: Part1.5V, M1.pin3, M2.pin3, M3.pin3, M6.pin3
  N2: Part1.D24, M1.pin1
  N3: Part1.D25, M2.pin1
  N4: Part1.D26, M3.pin1
  N5: Part1.D27, M4.pin1
  N6: Part1.D28, M5.pin1
  N7: Part1.D29, M6.pin1
  N8: Part1.GND, M1.pin2, M2.pin2, M3.pin2, M4.pin2, M5.pin2, M6.pin2
  N9: M4.pin3, M5.pin3
