# Fritzing sketch DCC-EX ESP32 Dev kit (saved by Fritzing 0.9.3b)

parts:
  Part1 = Arduino Motor Shield (Rev3)
  U2 = ESP32-38PinWide [part_number=ESP32-38PinWide]

nets:
  N1: Part1.A2, U2.GPIO35
  N2: Part1.A3, U2.GPIO34
  N3: Part1.D8/BreakeB, U2.GPIO12
  N4: Part1.D9/BreakeA, U2.GPIO13
  N5: Part1.D11_PWM/B, U2.GPIO23
  N6: Part1.D12/DirA, U2.GPIO19
  N7: Part1.D13/DirB, U2.GPIO18
  N8: Part1.D3_PWM/A, U2.GPIO25
  N9: Part1.IOREF, U2.3.3
  5V: Part1.5V, U2.VIN
  N10: Part1.GND, U2.GPIO11

custom parts:
  ESP32-38PinWide: Generic 38-Pin ESP32 with wide format (only access to one side of pins on a breadboard) based on Stephen Lilley's HiLetgo ESP-WROOM-32 ESP32 ESP-32S Development Board.
