# Fritzing sketch EX-Turntable with NEMA Stepper and A4988 (saved by Fritzing 0.9.10b)

parts:
  Mod1 = Nano-V3-0-IO-Expansion-Adapter
  M2 = Stepper Motor - Unipolar  # not connected
  C1 = Electrolytic Capacitor [capacitance=47µF voltage=35V package="300 mil [THT, electrolytic]"]
  Pololu_A1 = Pololu A4988 [package=SO16]

nets:
  N1: Mod1.A0, Pololu_A1.STEP
  N2: Mod1.A1, Pololu_A1.DIR
  N3: Mod1.A2, Pololu_A1.ENABLE
  VCC: Mod1.VCC, Pololu_A1.VDD
  N4: Mod1.GND, Pololu_A1.GND#8
  N5: C1.-, Pololu_A1.GND#14
  N6: C1.+, Pololu_A1.VMOT
  N7: Pololu_A1.RESET, Pololu_A1.SLEEP

notes:
  12V DC for stepper power
  47uF Electrolytic capacitor

custom parts:
  Nano-V3-0-IO-Expansion-Adapter: Nano V3.0 IO Expansion Adapter Shield. Note pcb view has been supressed as not useful. You can drag a Nano over the Nano connectors and it will connect and appear in schematic (although at present due to a bug, routing will not show as complete in breadboard).
