# Fritzing sketch EX-Turntable with NEMA Stepper and DRV8825 (saved by Fritzing 0.9.10b)

parts:
  Mod1 = Nano-V3-0-IO-Expansion-Adapter
  DRV_1 = DRV 8825 Stepper Motor Carrier, High Current [part_number="DRV 8825"]
  M2 = Stepper Motor - Unipolar
  C1 = Electrolytic Capacitor [capacitance=47µF voltage=35V package="300 mil [THT, electrolytic]"]

nets:
  N1: Mod1.A2, DRV_1.ENABLE
  N2: Mod1.A0, DRV_1.STEP
  N3: Mod1.A1, DRV_1.DIRECTION
  N4: Mod1.VCC, DRV_1.VOLTAGE_DD
  N5: Mod1.GND, DRV_1.GROUND_LOG
  N6: DRV_1.VOLTAGE_ST/_MT, C1.+
  N7: DRV_1.GROUND_ST/_MT, C1.-
  N8: DRV_1.OUT_2B, M2.A
  N9: DRV_1.OUT_2A, M2.C
  N10: DRV_1.OUT_1A, M2.B
  N11: DRV_1.OUT_1B, M2.D

notes:
  12V DC for stepper power
  47uF Electrolytic capacitor

custom parts:
  Nano-V3-0-IO-Expansion-Adapter: Nano V3.0 IO Expansion Adapter Shield. Note pcb view has been supressed as not useful. You can drag a Nano over the Nano connectors and it will connect and appear in schematic (although at present due to a bug, routing will not show as complete in breadboard).
