# Fritzing sketch Mega 2560 Pro mini (saved by Fritzing 0.9.3b)

parts:
  Mega2560_Pro_Mini1 = Mega2560 R3 Pro Mini
  Part1 = Arduino Motor Shield (Rev3)
  U1 = ESP8266 ESP-01 Upgraded WiFi Module [part_number=ESP8266]

nets:
  N1: Mega2560_Pro_Mini1.A1, Part1.A1
  N2: Mega2560_Pro_Mini1.A0, Part1.A0
  N3: Mega2560_Pro_Mini1.3▀, Part1.D3_PWM/A
  N4: Mega2560_Pro_Mini1.9▀, Part1.D9/BreakeA
  N5: Mega2560_Pro_Mini1.11▀, Part1.D11_PWM/B
  N6: Mega2560_Pro_Mini1.13▀, Part1.D13/DirB
  N7: Mega2560_Pro_Mini1.15, U1.RXD
  N8: Mega2560_Pro_Mini1.14, U1.TXD
  N9: Mega2560_Pro_Mini1.12▀, Part1.D12/DirA
  N10: Mega2560_Pro_Mini1.10▀, Part1.D10_PWM
  N11: Mega2560_Pro_Mini1.8▀, Part1.D8/BreakeB
  GND: Mega2560_Pro_Mini1.GND, Part1.GND, U1.GND
  5V: Mega2560_Pro_Mini1.5V, Part1.5V
  3V3: Mega2560_Pro_Mini1.3V3, U1.VCC, U1.CH_PD

custom parts:
  Mega2560 R3 Pro Mini: The Mega 2560 R3 Pro Mini :- Completely compatible with original Arduino Mega2560 Pin pitch: 0.1 inch Size: 5.42cm*3.68cm With Atmega16U2 chip as the USB to Serial converter 5V working voltage. Input Voltage:7-12V Analog Input Pins: 16 Digital I/O pins: 54 The Mega 2560 R3 Pro Mini has no datasheet and no info and I don't have one to compare, so I made this based on photos. Use it at your own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
  ESP8266 ESP-01 Upgraded WiFi Module: Upgraded Version ESP-01,all Flash are upgraded to 1M byte.Also support Cloud service remote transmission.
