# Fritzing sketch ex-ioexpander-mega (saved by Fritzing 0.9.10b)

parts:
  Part1 = Arduino Mega 2560 (Rev3)
  Part2 = Arduino Mega 2560 (Rev3)

nets:
  N1: Part1.D21/SCL, Part1.SCL, Part2.D21/SCL
  N2: Part1.D20/SDA, Part1.SDA, Part2.D20/SDA
  GND: Part1.GND, Part2.GND
