# Fritzing sketch ex-ioexpander-nano (saved by Fritzing 0.9.10b)

parts:
  Part1 = Arduino Mega 2560 (Rev3)
  Part2 = Arduino Nano (Rev3.0)

nets:
  N1: Part1.D21/SCL, Part2.A5
  N2: Part1.D20/SDA, Part2.A4
  GND: Part1.GND, Part2.GND
