# Fritzing sketch l293d-single-coil-turnouts (saved by Fritzing 0.9.10b)
breadboards: 1

parts:
  Part1 = Arduino Mega 2560 (Rev3)
  IC1 = L293D [package=THT]
  R1 = Resistor [tolerance=±5% power=0.25 resistance=10k package=THT]
  R2 = Resistor [tolerance=±5% power=0.25 resistance=10k package=THT]

nets:
  N1: Part1.5V, IC1.+V
  N2: Part1.D22, IC1.Enable_1, R1.Pin_0
  N3: Part1.D23, IC1.Enable_2, R2.Pin_1
  N4: Part1.D24, IC1.In_1
  N5: Part1.D25, IC1.In_3
  N6: Part1.D26, IC1.In_2
  N7: Part1.D27, IC1.In_4
  N8: Part1.GND, IC1.0V, R1.Pin_1, R2.Pin_0

notes:
  External Power
