# Fritzing sketch mega-cs-with-hc-05 (saved by Fritzing 0.9.10b)

parts:
  Part2 = Bluetooth HC-05 Macho
  R1 = Resistor [tolerance=±5% power=0.25 resistance=1k package=THT]
  R2 = Resistor [tolerance=±5% power=0.25 resistance=2k package=THT]
  Part3 = Arduino Mega 2560 (Rev3)

nets:
  N1: Part2.TXD, Part3.D19/RX1
  N2: Part2.RXD, R1.Pin_0, R2.Pin_0
  VCC: Part2.VCC, Part3.5V
  GND: Part2.GND, Part3.GND
  N3: R1.Pin_1, Part3.D18/TX1

notes:
  1K
  2K
