# Fritzing sketch mega-esp32-serial-connection (saved by Fritzing 0.9.10b)

parts:
  Part1 = Arduino Mega 2560 (Rev3)
  U1 = ESP32-38PinWide [part_number=ESP32-38PinWide]
  R2 = Resistor [tolerance=±5% power=0.25 resistance=2 package=THT]
  R3 = Resistor [tolerance=±5% power=0.25 resistance=1k package=THT]

nets:
  N1: Part1.D17_PWM/RX2, U1.GPIO32
  N2: Part1.D16_PWM/TX2, R3.Pin_1
  N3: Part1.GND, U1.GPIO11, R2.Pin_0
  N4: U1.GPIO33, R2.Pin_1, R3.Pin_0

custom parts:
  ESP32-38PinWide: Generic 38-Pin ESP32 with wide format (only access to one side of pins on a breadboard) based on Stephen Lilley's HiLetgo ESP-WROOM-32 ESP32 ESP-32S Development Board.
