# Fritzing sketch mega-for-flashing-makerfabs-wifi-simple-jumpers (saved by Fritzing 0.9.3b)

parts:
  Part3 = Arduino Mega 2560 (Rev3)
  Part1 = Makerfabs WiFi Shield

nets:
  N1: Part3.A0, Part1.Pin_7
  N2: Part3.A1, Part1.Pin_8
  N3: Part3.A2, Part1.Pin_9
  N4: Part3.A3, Part1.Pin_10
  N5: Part3.A4, Part1.Pin_11
  N6: Part3.A5, Part1.Pin_12
  N7: Part3.AREF, Part3.D2_PWM, Part1.Pin_45, Part1.Pin_58
  N8: Part3.GND, Part3.RESET, Part1.Pin_1, Part1.Pin_4, Part1.Pin_5, Part1.Pin_57
  N9: Part3.D13_PWM, Part1.Pin_56
  N10: Part3.D12_PWM, Part1.Pin_55
  N11: Part3.D11_PWM, Part1.Pin_54
  N12: Part3.D10_PWM, Part1.Pin_53
  N13: Part3.D9_PWM, Part1.Pin_52
  N14: Part3.D8_PWM, Part1.Pin_51
  N15: Part3.3V3, Part1.Pin_2
  N16: Part3.5V, Part1.Pin_3
  N17: Part3.VIN, Part1.Pin_6
  N18: Part3.D0_RX0, Part1.Pin_43
  N19: Part3.D1_TX0, Part1.Pin_44
  N20: Part3.D3_PWM, Part1.Pin_46
  N21: Part3.D4_PWM, Part1.Pin_47
  N22: Part3.D5_PWM, Part1.Pin_48
  N23: Part3.D6_PWM, Part1.Pin_49
  N24: Part3.D7_PWM, Part1.Pin_50
  N25: Part1.Pin_19, Part1.Pin_27
  N26: Part1.Pin_28, Part1.Pin_36

custom parts:
  Makerfabs WiFi Shield: Arduino Zero is a simple and powerful 32-bit extension of the platform established by Arduino UNO. The Zero board aims to provide creative individuals with the potential to realize truly innovative ideas for smart IoT devices, wearable technology, high-tech automation, crazy robotics, and projects not yet imagined. The board is powered by Atmel’s SAMD21 MCU, which features a 32-bit ARM Cortex®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
