# Fritzing sketch mega-for-flashing-makerfabs-wifi (saved by Fritzing 0.9.3b)

parts:
  Part1 = Makerfabs WiFi Shield
  Part3 = Arduino Mega 2560 (Rev3)

nets:
  N1: Part1.Pin_1, Part1.Pin_4, Part1.Pin_5, Part1.Pin_57, Part3.GND, Part3.RESET
  N2: Part1.Pin_2, Part3.3V3
  N3: Part1.Pin_3, Part3.5V
  N4: Part1.Pin_6, Part3.VIN
  N5: Part1.Pin_7, Part3.A0
  N6: Part1.Pin_8, Part3.A1
  N7: Part1.Pin_9, Part3.A2
  N8: Part1.Pin_10, Part3.A3
  N9: Part1.Pin_11, Part3.A4
  N10: Part1.Pin_12, Part3.A5
  N11: Part1.Pin_26, Part1.Pin_44, Part3.D1_TX0
  N12: Part1.Pin_42, Part1.Pin_43, Part3.D0_RX0
  N13: Part1.Pin_45, Part1.Pin_58, Part3.AREF, Part3.D2_PWM
  N14: Part1.Pin_46, Part3.D3_PWM
  N15: Part1.Pin_47, Part3.D4_PWM
  N16: Part1.Pin_48, Part3.D5_PWM
  N17: Part1.Pin_49, Part3.D6_PWM
  N18: Part1.Pin_50, Part3.D7_PWM
  N19: Part1.Pin_51, Part3.D8_PWM
  N20: Part1.Pin_52, Part3.D9_PWM
  N21: Part1.Pin_53, Part3.D10_PWM
  N22: Part1.Pin_54, Part3.D11_PWM
  N23: Part1.Pin_55, Part3.D12_PWM
  N24: Part1.Pin_56, Part3.D13_PWM

custom parts:
  Makerfabs WiFi Shield: Arduino Zero is a simple and powerful 32-bit extension of the platform established by Arduino UNO. The Zero board aims to provide creative individuals with the potential to realize truly innovative ideas for smart IoT devices, wearable technology, high-tech automation, crazy robotics, and projects not yet imagined. The board is powered by Atmel’s SAMD21 MCU, which features a 32-bit ARM Cortex®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
