# Fritzing sketch mega-with-i2c-oled-twi (saved by Fritzing 0.9.10b)

parts:
  o1 = Module display OLED I2C 128x64 SSD1306 [package=THT]
  Part1 = Arduino Mega 2560 (Rev3)  # not connected
  Part2 = Arduino Motor Shield (Rev3)

nets:
  GND: o1.GND, Part2.GND
  VCC: o1.VCC, Part2.5V
  N1: o1.SCL, Part2.SCL
  N2: o1.SDA, Part2.SDA

custom parts:
  Module display OLED I2C 128x64 SSD1306: Ecran OLED I2C SSD163 de 128x64 avec connexion I2C
