# Fritzing sketch mega-with-ir-sensor (saved by Fritzing 0.9.3b)

parts:
  Part1 = Arduino Mega ADK (Rev3)
  M1 = fc-51 [package=THT]

nets:
  N1: Part1.5V, M1.pin3
  N2: Part1.GND, M1.pin2
  N3: Part1.D22, M1.pin1
