# Fritzing sketch mega2560-dual-vl53l0x (saved by Fritzing 0.9.10b)

parts:
  Part1 = Arduino Mega 2560 (Rev3)
  Part2 = Adafruit VL530X Time of Flight Distance Sensor [part_number="Adafruit #3317"]
  Part3 = Adafruit VL530X Time of Flight Distance Sensor [part_number="Adafruit #3317"]
  A1 = Mcp23017 Interface Module [package=THT]

nets:
  N1: Part1.D21/SCL, Part2.SCL, Part3.SCL, A1.Pin_23
  N2: Part1.D20/SDA, Part2.SDA, Part3.SDA, A1.Pin_24
  VCC: Part1.5V, Part2.VCC, Part3.VCC, A1.Pin_21
  N3: Part1.D22, Part2.XSHUT
  GND: Part1.GND, Part2.GND, Part3.GND, A1.Pin_1, A1.Pin_22
  N4: Part3.XSHUT, A1.Pin_3

custom parts:
  Adafruit VL530X Time of Flight Distance Sensor: The VL53L0X is a Time of Flight distance sensor like no other you've used! The sensor contains a very tiny invisible laser source, and a matching sensor. The VL53L0X can detect the "time of flight", or how long the light has taken to bounce back to the sensor. Since it uses a very narrow light source, it is good for determining distance of only the surface directly in front of it. Unlike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
  Mcp23017 Interface Module: The MCP23017 is capable of converting 16-bit parallel data to serial data of the IIC interface and converting each other. An internal integrated power-on reset (POR) circuit is reset to the device's default state. The two opposites become the interrupt source output. The polarity toggle register configures the GPIO input polarity.
