# Fritzing sketch mega2560-multiplexer-example (saved by Fritzing 0.9.10b)

parts:
  Part1 = Arduino Mega 2560 (Rev3)
  Part2 = Adafruit TCA9548A
  A1 = Mcp23017 Interface Module [package=THT]
  A2 = Mcp23017 Interface Module [package=THT]

nets:
  N1: Part1.D21/SCL, Part2.INPUTSCL
  N2: Part1.D20/SDA, Part2.INPUTSDA
  GND: Part1.GND, Part2.GND, A1.Pin_1, A1.Pin_22, A2.Pin_22
  5V: Part1.5V, Part2.VCC, A1.Pin_11, A1.Pin_21, A2.Pin_11, A2.Pin_21
  N3: Part2.2SDA, A2.Pin_24
  N4: Part2.2SCL, A2.Pin_23
  N5: Part2.3SDA, A1.Pin_24
  N6: Part2.3SCL, A1.Pin_23

custom parts:
  Adafruit TCA9548A: You just found the perfect I2C sensor, and you want to wire up two or three or more of them to your Arduino when you realize "Uh oh, this chip has a fixed I2C address, and from what I know about I2C, you cannot have two devices with the same address on the same SDA/SCL pins!" Are you out of luck? You would be, if you didn't have this ultra-cool TCA9548A 1-to-8 I2C multiplexer! Finally, a way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
  Mcp23017 Interface Module: The MCP23017 is capable of converting 16-bit parallel data to serial data of the IIC interface and converting each other. An internal integrated power-on reset (POR) circuit is reset to the device's default state. The two opposites become the interrupt source output. The polarity toggle register configures the GPIO input polarity.
