# Fritzing sketch mega2560-single-vl53l0x (saved by Fritzing 0.9.10b)

parts:
  Part1 = Arduino Mega 2560 (Rev3)
  Part2 = Adafruit VL530X Time of Flight Distance Sensor [part_number="Adafruit #3317"]

nets:
  N1: Part1.D21/SCL, Part2.SCL
  N2: Part1.D20/SDA, Part2.SDA
  5V: Part1.5V, Part2.VCC, Part2.GPIO
  GND: Part1.GND, Part2.GND

custom parts:
  Adafruit VL530X Time of Flight Distance Sensor: The VL53L0X is a Time of Flight distance sensor like no other you've used! The sensor contains a very tiny invisible laser source, and a matching sensor. The VL53L0X can detect the "time of flight", or how long the light has taken to bounce back to the sensor. Since it uses a very narrow light source, it is good for determining distance of only the surface directly in front of it. Unlike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
