# Fritzing sketch nano-hc-bluetooth-programmer (saved by Fritzing 0.9.10b)

parts:
  Part1 = Arduino Nano (Rev3.0)
  Part2 = Bluetooth HC-05 Macho
  R1 = Resistor [tolerance=±5% power=0.25 resistance=1k package=THT]
  R2 = Resistor [tolerance=±5% power=0.25 resistance=2k package=THT]

nets:
  N1: Part1.D2, Part2.TXD
  N2: Part1.D3, R1.Pin_1
  N3: Part1.D4, Part2.Key
  GND: Part1.GND, Part2.GND
  5V: Part1.5V, Part2.VCC
  N4: Part2.RXD, R1.Pin_0, R2.Pin_0

notes:
  1K
  2K
