# Fritzing sketch signal-4aspect-active-low (saved by Fritzing 0.9.10b)

parts:
  Part1 = Arduino Mega 2560 (Rev3)
  R3 = Resistor [tolerance=±5% power=0.25 resistance=220 package=THT]
  R2 = Resistor [tolerance=±5% power=0.25 resistance=220 package=THT]
  R1 = Resistor [tolerance=±5% power=0.25 resistance=220 package=THT]
  R4 = Resistor [tolerance=±5% power=0.25 resistance=220 package=THT]

nets:
  N1: Part1.D28, R1.Pin_0
  N2: Part1.D30, R2.Pin_0
  N3: Part1.D32, R3.Pin_0
  N4: Part1.D34, R4.Pin_1
